// Logisim project main_cpu.circ as structural Verilog: 1 circuit, main circuit CPU
module CPU (
);

  wire AE, and_2_out, and_3_out, and_4_out, and_6_out, and_8_out, AS, clock_1_out, DA, demultiplexer_1_out0,
       demultiplexer_1_out1, demultiplexer_1_out2, demultiplexer_1_out3, GC, IA, M, n74193_1_pin1,
       n74193_1_pin4, not_1_out, not_2_out, not_3_out, not_4_out, not_5_out, not_6_out, not_7_out, not_8_out,
       not_9_out, not_10_out, or_6_out, PC_pin4, PC_pin12, register_1_q;
  wire [1:0] and_9_out, demultiplexer_3_out0, demultiplexer_3_out1, IR_q_3, n74193_1_pin3, n74193_1_pin6;
  wire [2:0] and_13_out, IR_q, register_2_q;
  wire [2:2] or_2_out;
  wire [5:3] IR_q_2;
  wire [7:0] ACC_q, adder_1_out, and_10_out, demultiplexer_2_out0, demultiplexer_2_out1,
       demultiplexer_2_out2, demultiplexer_2_out3, divider_1_out, divider_1_rem, MAR_q, multiplexer_1_out,
       multiplexer_2_out, multiplexer_3_out, multiplexer_4_out, multiplier_1_out, or_4_out, PC_pin3,
       ram_1_dout, REGA_q, REGB_q, rom_1_data, subtractor_1_out, xor_1_out;

  and and_1 (AS, M, DA);
  or or_1 (AE, AS, IA);
  and and_2 (and_2_out, IR_q[2], not_9_out);
  Register #(.trigger("falling"), .width(1)) register_1 (
    .D(and_6_out), .clk(clock_1_out), .Q(register_1_q));  // open: en, clr
  or or_2 (or_2_out[2], and_3_out, and_2_out);
  or or_3 (and_9_out[1], and_4_out, and_8_out);
  and and_3 (and_3_out, IA, IR_q_3[0]);
  and and_4 (and_4_out, IA, IR_q_3[1]);
  ROM rom_1 (.addr(PC_pin3), .data(rom_1_data));
  Clock clock_1 (.out(clock_1_out));
  and and_5 (GC, clock_1_out, not_1_out);
  not not_1 (not_1_out, register_1_q);
  not not_2 (not_2_out, IR_q_3[0]);
  not not_3 (not_3_out, IR_q_2[5]);
  not not_4 (not_4_out, IR_q_2[4]);
  and and_6 (and_6_out, IR_q_3[1], not_2_out, not_3_out, not_4_out, not_5_out, not_6_out, not_7_out, not_8_out);
  not not_5 (not_5_out, IR_q_2[3]);
  not not_6 (not_6_out, IR_q[2]);
  not not_7 (not_7_out, IR_q[1]);
  not not_8 (not_8_out, IR_q[0]);
  Register REGA (.D(demultiplexer_2_out1), .en(demultiplexer_1_out1), .clk(GC), .Q(REGA_q));  // open: clr
  Register REGB (.D(demultiplexer_2_out0), .en(demultiplexer_1_out0), .clk(GC), .Q(REGB_q));  // open: clr
  and and_7 (DA, and_8_out, and_9_out[0]);
  and and_8 (and_8_out, IR_q[1], not_9_out);
  and and_9 (and_9_out[0], IR_q[0], not_9_out);
  Register IR (.D(rom_1_data), .clk(GC), .Q({IR_q_3, IR_q_2, IR_q}));  // open: en, clr
  Adder adder_1 (.a(REGA_q), .b(REGB_q), .out(adder_1_out));  // open: cin, cout
  Subtractor subtractor_1 (.a(REGA_q), .b(REGB_q), .out(subtractor_1_out));  // open: bin, bout
  Multiplier multiplier_1 (.a(REGA_q), .b(REGB_q), .out(multiplier_1_out));  // open: cin, cout
  Divider divider_1 (.a(REGA_q), .b(REGB_q), .out(divider_1_out), .rem(divider_1_rem));  // open: upper
  assign and_10_out = REGA_q & REGB_q;  // AND_Gate and_10, 8 bits wide
  assign or_4_out = REGA_q | REGB_q;  // OR_Gate or_4, 8 bits wide
  assign xor_1_out = REGA_q ^ REGB_q;  // XOR_Gate xor_1, 8 bits wide
  not not_9 (not_9_out, IA);
  nor nor_1 (IA, IR_q_2[5], IR_q_2[4], IR_q_2[3]);
  and and_11 (and_13_out[2], IA, IR_q[2]);
  not not_10 (not_10_out, GC);
  and and_12 (and_13_out[1], IA, IR_q[1]);
  and and_13 (and_13_out[0], IA, IR_q[0]);
  _74193 PC (
    .pin2(PC_pin3[1]), .pin3(PC_pin3[0]), .pin4(PC_pin4), .pin5(GC), .pin6(PC_pin3[2]), .pin7(PC_pin3[3]),
    .pin12(PC_pin12));  // open: pin1, pin15, pin14, pin13, pin11, pin10, pin9
  Register MAR (.D(demultiplexer_2_out2), .en(demultiplexer_1_out2), .clk(GC), .Q(MAR_q));  // open: clr
  Register ACC (.D(multiplexer_2_out), .en(AE), .clk(GC), .Q(ACC_q));  // open: clr
  // Probe on multiplexer_1_out
  Multiplexer #(.select(3), .width(8)) multiplexer_1 (
    .in0(adder_1_out), .in1(subtractor_1_out), .in2(multiplier_1_out), .in3(divider_1_out),
    .in4(divider_1_rem), .in5(and_10_out), .in6(or_4_out), .in7(xor_1_out), .out(multiplexer_1_out),
    .sel(register_2_q));
  Multiplexer #(.width(8)) multiplexer_2 (
    .in0(multiplexer_1_out), .in1(demultiplexer_2_out3), .out(multiplexer_2_out), .sel(AS));
  Register #(.trigger("falling"), .width(3)) register_2 (
    .D(and_13_out), .en(IA), .clk(clock_1_out), .Q(register_2_q));  // open: clr
  _74193 u_74193_1 (
    .pin1(n74193_1_pin1), .pin2(n74193_1_pin3[1]), .pin3(n74193_1_pin3[0]), .pin4(n74193_1_pin4), .pin5(IA),
    .pin6(n74193_1_pin6[0]), .pin7(n74193_1_pin6[1]), .pin15(PC_pin4), .pin11(not_10_out),
    .pin10(n74193_1_pin1), .pin9(n74193_1_pin1));  // open: pin14, pin13, pin12
  _74193 PC_1 (
    .pin2(PC_pin3[5]), .pin3(PC_pin3[4]), .pin4(PC_pin4), .pin5(PC_pin12), .pin6(PC_pin3[6]),
    .pin7(PC_pin3[7]));  // open: pin1, pin15, pin14, pin13, pin12, pin11, pin10, pin9
  RAM ram_1 (.addr(MAR_q), .we(IR_q_2[3]), .oe(IR_q_2[4]), .clk(GC), .din(ACC_q), .dout(ram_1_dout));
  or or_5 (M, IR_q_2[5], IA);
  // Probe on ACC_q
  or or_6 (or_6_out, n74193_1_pin6[1], n74193_1_pin6[0], n74193_1_pin3[1], n74193_1_pin3[0]);
  and and_14 (n74193_1_pin4, or_6_out, GC);
  Button #(.press("passive")) button_1 (.out(PC_pin4));
  Multiplexer #(.enable("true"), .select(2), .width(8)) multiplexer_3 (
    .in0(REGB_q), .in1(REGA_q), .in2(MAR_q), .in3(ram_1_dout), .out(multiplexer_3_out),
    .sel(demultiplexer_3_out0), .en(M));
  // AND_Gate and_15 has open pins: in0=demultiplexer_1_out3, in1=GC, out=open
  // NOT_Gate not_11 has open pins: in=or_6_out, out=open
  Demultiplexer #(.enable("true"), .select(2)) demultiplexer_1 (
    .out0(demultiplexer_1_out0), .out1(demultiplexer_1_out1), .out2(demultiplexer_1_out2),
    .out3(demultiplexer_1_out3), .in(M), .sel(and_9_out), .en(M));
  Demultiplexer #(.enable("true"), .select(2), .width(8)) demultiplexer_2 (
    .out0(demultiplexer_2_out0), .out1(demultiplexer_2_out1), .out2(demultiplexer_2_out2),
    .out3(demultiplexer_2_out3), .in(multiplexer_4_out), .sel(and_9_out), .en(M));
  Multiplexer #(.width(8)) multiplexer_4 (
    .in0(multiplexer_3_out), .in1({{6{1'b0}}, demultiplexer_3_out1}), .out(multiplexer_4_out),
    .sel(or_2_out[2]));
  Demultiplexer #(.width(2)) demultiplexer_3 (
    .out0(demultiplexer_3_out0), .out1(demultiplexer_3_out1), .in(IR_q_3), .sel(or_2_out[2]));
  // Probe on ram_1_dout
  // also tied to GND on the sheet: n74193_1_pin1

  // Notes on the sheet:
  //   contents of rom_1 (hex, n*v repeats v):
  //   65 64 0 8 10 e1 1 66 8 66 10 26 e3 10 8 66 e3 8 0 e6 8 a4 2 a6 8 10 e6 e3 10 8 a6 e3 8 80 80
endmodule
